# Fritzing sketch pcb (saved by Fritzing 0.9.5d)
circuit board: 5.99038cm x 5.18151cm
breadboards: 1

parts:
  ATtiny = attiny85 [package=dip]
  L293D = L293D [package=THT]
  PFET = MOSFET-NCHANNEL [package=to-92]
  NFET = MOSFET-NCHANNEL [package=to-92]
  MOUT1 = male pin header, 1 pin [form="♂ (male)"]
  MOUT2 = male pin header, 1 pin [form="♂ (male)"]
  LDO = male pin header, 1 pin [form="♂ (male)"]
  LCLK = male pin header, 1 pin [form="♂ (male)"]
  ISP = male pin header, 3 pins [form="♂ (male)"]
  R1 = Resistor [tolerance=±5% resistance=220 package=THT]
  Power = Screw terminal - 2 pins [package=THT]
  LEDP = male pin header, 2 pins [form="♂ (male)"]
  BIN = male pin header, 1 pin [form="♂ (male)"]
  BVCC = male pin header, 1 pin [form="♂ (male)"]
  ISP_2 = male pin header, 3 pins [form="♂ (male)"]

nets:
  N1: ATtiny.Pin_1, ISP.pin3
  N2: ATtiny.Pin_2, R1.Pin_0, BIN.pin1
  N3: ATtiny.Pin_3, L293D.Enable_1
  N4: ATtiny.Pin_4, L293D.0V, NFET.G, R1.Pin_1, Power.pin1, LEDP.pin1, ISP_2.pin3
  N5: ATtiny.Pin_5, L293D.In_1, PFET.S, NFET.S, ISP_2.pin2
  N6: ATtiny.Pin_6, LDO.pin1, ISP.pin1
  N7: ATtiny.Pin_7, LCLK.pin1, ISP.pin2
  N8: ATtiny.Pin_8, L293D.+Vmotor, L293D.+V, PFET.D, Power.pin2, LEDP.pin2, BVCC.pin1, ISP_2.pin1
  N9: L293D.Out_1_(_Controlled_by_Enable_1_), MOUT1.pin1
  N10: L293D.Out_2_(_Controlled_by_Enable_1_), MOUT2.pin1
  N11: L293D.In_2, PFET.G, NFET.D
