# Fritzing sketch perfboardlayout (saved by Fritzing 0.9.5d)
perfboards: 1

parts:
  IC1 = L293D [package=THT]
  U1 = attiny85 [package=dip]
  J1 = female pin header, 2 pins [form="♀ (female)"]
  R1 = Resistor [tolerance=±5% resistance=220 package=THT]
  J2 = male pin header, 2 pins [form="♂ (male)"]
  J3 = male pin header, 2 pins [form="♂ (male)"]
  J4 = male pin header, 2 pins [form="♂ (male)"]
  Q1 = PNP-Transistor [package="TO92 [THT]"]  # not connected
  Q2 = NPN-Transistor [package="TO92 [THT]"]  # not connected
  J5 = rounded female pin header, 3 pins [form="♀ (female rounded)"]
  J6 = rounded female pin header, 3 pins [form="♀ (female rounded)"]
  J8 = male pin header, 2 pins [form="♂ (male)"]
  J7 = male pin header, 4 pins [form="♂ (male)"]
  J9 = male pin header, 2 pins [form="♂ (male)"]

nets:
  N1: IC1.Enable_1, U1.Pin_3
  N2: IC1.In_1, U1.Pin_6, J2.pin1, J5.pin2, J6.pin2, J7.pin3
  N3: IC1.Out_1_(_Controlled_by_Enable_1_), J8.pin1
  N4: IC1.0V, U1.Pin_4, J1.pin1, R1.Pin_1, J4.pin2, J7.pin1
  N5: IC1.Out_2_(_Controlled_by_Enable_1_), J8.pin2
  N6: IC1.In_2, J6.pin1
  N7: IC1.+Vmotor, IC1.+V, U1.Pin_8, J1.pin2, J7.pin4
  N8: U1.Pin_1, J4.pin1
  N9: U1.Pin_2, R1.Pin_0, J9.pin2
  N10: U1.Pin_5, J3.pin2
  N11: U1.Pin_7, J3.pin1, J7.pin2
  N12: J5.pin1, J6.pin3
